// Logisim project Memory-Project.circ as structural Verilog: 12 circuits, main circuit main
module main (
);

  wire clock_1_out;

  Clock clock_1 (.out(clock_1_out));
  D_Flip_Flop #(.trigger("falling")) d_ff_1 (.clk(clock_1_out));  // open: D, Q, Qn, preset, en, reset
  D_Flip_Flop #(.trigger("falling")) d_ff_2 ();  // open: clk, D, Q, Qn, preset, en, reset
  D_Flip_Flop #(.trigger("falling")) d_ff_3 ();  // open: clk, D, Q, Qn, preset, en, reset
  D_Flip_Flop #(.trigger("falling")) d_ff_4 ();  // open: clk, D, Q, Qn, preset, en, reset
  D_Flip_Flop #(.trigger("falling")) d_ff_5 ();  // open: clk, D, Q, Qn, preset, en, reset
  D_Flip_Flop #(.trigger("falling")) d_ff_6 ();  // open: clk, D, Q, Qn, preset, en, reset
  D_Flip_Flop #(.trigger("falling")) d_ff_7 ();  // open: clk, D, Q, Qn, preset, en, reset
  D_Flip_Flop #(.trigger("falling")) d_ff_8 ();  // open: clk, D, Q, Qn, preset, en, reset
  D_Flip_Flop #(.trigger("falling")) d_ff_9 ();  // open: clk, D, Q, Qn, preset, en, reset
  D_Flip_Flop #(.trigger("falling")) d_ff_10 ();  // open: clk, D, Q, Qn, preset, en, reset
  D_Flip_Flop #(.trigger("falling")) d_ff_11 ();  // open: clk, D, Q, Qn, preset, en, reset
  D_Flip_Flop #(.trigger("falling")) d_ff_12 ();  // open: clk, D, Q, Qn, preset, en, reset
endmodule

module finite_state_machine (
);

  wire and_1_out, and_2_out, and_3_out, comparator_1_gt, comparator_2_lt, comparator_3_gt, comparator_4_lt,
       comparator_5_lt, comparator_6_gt, comparator_7_lt, comparator_8_gt, comparator_9_lt, comparator_10_gt,
       or_1_out;
  wire [11:0] counter_2_output, counter_output;

  counter counter (.D_input(12'h1c), .\output (counter_output));
  counter counter_2 (.D_input(12'h1c), .\output (counter_2_output));
  Comparator #(.width(12)) comparator_1 (.a(12'h8), .b(counter_output), .gt(comparator_1_gt));  // open: eq, lt
  Comparator #(.width(12)) comparator_2 (.a(12'h7), .b(counter_output), .lt(comparator_2_lt));  // open: gt, eq
  Comparator #(.width(12)) comparator_3 (.a(12'hc), .b(counter_output), .gt(comparator_3_gt));  // open: eq, lt
  Comparator #(.width(12)) comparator_4 (.a(12'hb), .b(counter_output), .lt(comparator_4_lt));  // open: gt, eq
  Comparator #(.width(12)) comparator_5 (.a(12'hd), .b(counter_2_output), .lt(comparator_5_lt));  // open: gt, eq
  Comparator #(.width(12)) comparator_6 (.a(12'h16), .b(counter_2_output), .gt(comparator_6_gt));  // open: eq, lt
  Comparator #(.width(12)) comparator_7 (.a(12'h15), .b(counter_2_output), .lt(comparator_7_lt));  // open: gt, eq
  Comparator #(.width(12)) comparator_8 (.a(12'h1a), .b(counter_2_output), .gt(comparator_8_gt));  // open: eq, lt
  Comparator #(.width(12)) comparator_9 (.a(12'h19), .b(counter_2_output), .lt(comparator_9_lt));  // open: gt, eq
  Comparator #(.width(12)) comparator_10 (.a(12'he), .b(counter_2_output), .gt(comparator_10_gt));  // open: eq, lt
  and and_1 (and_1_out, comparator_2_lt, comparator_3_gt);
  and and_2 (and_2_out, comparator_5_lt, comparator_6_gt);
  and and_3 (and_3_out, comparator_7_lt, comparator_8_gt);
  or or_1 (or_1_out, comparator_9_lt, comparator_10_gt);
  LED green (.in(comparator_1_gt));
  LED yellow (.in(and_1_out));
  LED red (.in(comparator_4_lt));
  LED green_2 (.in(and_2_out));
  LED yellow_2 (.in(and_3_out));
  LED red_2 (.in(or_1_out));
endmodule

module counter (
  input  [11:0] D_input,
  output [11:0] \output 
);

  wire clock_out, comparator_1_gt, or_1_out;
  wire [11:0] complementary_2_12_bit_lookahead_adder_1_out_4;

  Comparator #(.width(12)) comparator_1 (.a(\output ), .b(D_input), .gt(comparator_1_gt));  // open: eq, lt
  Clock clock (.out(clock_out));
  complementary_2_12_bit_lookahead_adder complementary_2_12_bit_lookahead_adder_1 (
    .in_1(\output ), .in_3({12{1'b0}}), .in_2(1'b1), .out_4(complementary_2_12_bit_lookahead_adder_1_out_4));  // open: out_6, overflow
  or or_1 (or_1_out, \output [11], comparator_1_gt);
  _12_bit_Register u_12_bit_register_1 (
    .D(complementary_2_12_bit_lookahead_adder_1_out_4), .Reset(or_1_out), .Write(1'b1), .C(clock_out),
    .Q(\output ));
endmodule

module _12_bit_Register (
  input  [11:0] D,
  input  Reset,
  input  Write,
  input  C,
  output [11:0] Q
);

  D_Flip_Flop #(.trigger("falling")) d_ff_1 (
    .clk(C), .D(D[0]), .Q(Q[0]), .en(Write), .reset(Reset));  // open: Qn, preset
  D_Flip_Flop #(.trigger("falling")) d_ff_2 (
    .clk(C), .D(D[1]), .Q(Q[1]), .en(Write), .reset(Reset));  // open: Qn, preset
  D_Flip_Flop #(.trigger("falling")) d_ff_3 (
    .clk(C), .D(D[2]), .Q(Q[2]), .en(Write), .reset(Reset));  // open: Qn, preset
  D_Flip_Flop #(.trigger("falling")) d_ff_4 (
    .clk(C), .D(D[3]), .Q(Q[3]), .en(Write), .reset(Reset));  // open: Qn, preset
  D_Flip_Flop #(.trigger("falling")) d_ff_5 (
    .clk(C), .D(D[4]), .Q(Q[4]), .en(Write), .reset(Reset));  // open: Qn, preset
  D_Flip_Flop #(.trigger("falling")) d_ff_6 (
    .clk(C), .D(D[5]), .Q(Q[5]), .en(Write), .reset(Reset));  // open: Qn, preset
  D_Flip_Flop #(.trigger("falling")) d_ff_7 (
    .clk(C), .D(D[6]), .Q(Q[6]), .en(Write), .reset(Reset));  // open: Qn, preset
  D_Flip_Flop #(.trigger("falling")) d_ff_8 (
    .clk(C), .D(D[7]), .Q(Q[7]), .en(Write), .reset(Reset));  // open: Qn, preset
  D_Flip_Flop #(.trigger("falling")) d_ff_9 (
    .clk(C), .D(D[8]), .Q(Q[8]), .en(Write), .reset(Reset));  // open: Qn, preset
  D_Flip_Flop #(.trigger("falling")) d_ff_10 (
    .clk(C), .D(D[9]), .Q(Q[9]), .en(Write), .reset(Reset));  // open: Qn, preset
  D_Flip_Flop #(.trigger("falling")) d_ff_11 (
    .clk(C), .D(D[10]), .Q(Q[10]), .en(Write), .reset(Reset));  // open: Qn, preset
  D_Flip_Flop #(.trigger("falling")) d_ff_12 (
    .clk(C), .D(D[11]), .Q(Q[11]), .en(Write), .reset(Reset));  // open: Qn, preset
endmodule

module Register_File (
);

  _12_bit_Register u_12_bit_register_1 ();  // open: D, Reset, Write, C, Q
  _12_bit_Register u_12_bit_register_2 ();  // open: D, Reset, Write, C, Q
  _12_bit_Register u_12_bit_register_3 ();  // open: D, Reset, Write, C, Q
  _12_bit_Register u_12_bit_register_4 ();  // open: D, Reset, Write, C, Q
  _12_bit_Register u_12_bit_register_5 ();  // open: D, Reset, Write, C, Q
  _12_bit_Register u_12_bit_register_6 ();  // open: D, Reset, Write, C, Q
  _12_bit_Register u_12_bit_register_7 ();  // open: D, Reset, Write, C, Q
  _12_bit_Register u_12_bit_register_8 ();  // open: D, Reset, Write, C, Q
endmodule

module complementary_2_12_bit_lookahead_adder (
  input  [11:0] in_1,
  input  in_2,
  input  [11:0] in_3,
  output [11:0] out_4,
  output overflow,
  output out_6
);

  wire n4_bit_lookahead_adder_1_out_5, n4_bit_lookahead_adder_2_out_5, n4_bit_lookahead_adder_3_out_4;

  _4_bit_lookahead_adder u_4_bit_lookahead_adder_1 (
    .in_2({in_3[3], in_1[3], in_3[2], in_1[2], in_3[1], in_1[1], in_3[0], in_1[0]}), .in_1(in_2),
    .out_5(n4_bit_lookahead_adder_1_out_5), .out_3(out_4[3:0]));  // open: out_4
  _4_bit_lookahead_adder u_4_bit_lookahead_adder_2 (
    .in_2({in_3[7], in_1[7], in_3[6], in_1[6], in_3[5], in_1[5], in_3[4], in_1[4]}),
    .in_1(n4_bit_lookahead_adder_1_out_5), .out_5(n4_bit_lookahead_adder_2_out_5), .out_3(out_4[7:4]));  // open: out_4
  _4_bit_lookahead_adder u_4_bit_lookahead_adder_3 (
    .in_2({in_3[11], in_1[11], in_3[10], in_1[10], in_3[9], in_1[9], in_3[8], in_1[8]}),
    .in_1(n4_bit_lookahead_adder_2_out_5), .out_5(out_6), .out_3(out_4[11:8]),
    .out_4(n4_bit_lookahead_adder_3_out_4));
  xor xor_1 (overflow, n4_bit_lookahead_adder_3_out_4, out_6);
endmodule

module C1 (
  input  in_1,
  input  [7:0] in_2,
  output out_3
);

  wire and_1_out, g0_out, p0_out;

  and g0 (g0_out, in_2[1], in_2[0]);
  or p0 (p0_out, in_2[1], in_2[0]);
  and and_1 (and_1_out, in_1, p0_out);
  or or_1 (out_3, g0_out, and_1_out);
endmodule

module C2 (
  input  in_1,
  input  [7:0] in_2,
  output out_3
);

  wire and_1_out, and_2_out, g0_out, g1_out, p0_out, p1_out;

  or p0 (p0_out, in_2[0], in_2[1]);
  and g0 (g0_out, in_2[0], in_2[1]);
  or p1 (p1_out, in_2[2], in_2[3]);
  and g1 (g1_out, in_2[3], in_2[2]);
  and and_1 (and_1_out, in_1, p0_out, p1_out);
  and and_2 (and_2_out, g0_out, p1_out);
  or or_1 (out_3, and_1_out, and_2_out, g1_out);
endmodule

module C3 (
  input  in_1,
  input  [7:0] in_2,
  output out_3
);

  wire and_1_out, and_2_out, and_3_out, g0_out, g1_out, g2_out, p0_out, p1_out, p2_out;

  or p0 (p0_out, in_2[1], in_2[0]);
  and g0 (g0_out, in_2[1], in_2[0]);
  or p1 (p1_out, in_2[3], in_2[2]);
  and g1 (g1_out, in_2[3], in_2[2]);
  or p2 (p2_out, in_2[5], in_2[4]);
  and g2 (g2_out, in_2[5], in_2[4]);
  and and_1 (and_1_out, in_1, p0_out, p1_out, p2_out);
  and and_2 (and_2_out, g0_out, p1_out, p2_out);
  and and_3 (and_3_out, g1_out, p2_out);
  or or_1 (out_3, and_1_out, and_2_out, and_3_out, g2_out);
endmodule

module C4 (
  input  C0,
  input  [7:0] in_2,
  output C4
);

  wire and_1_out, and_2_out, and_3_out, and_4_out, g0_out, g1_out, g2_out, g3_out, p0_out, p1_out, p2_out,
       p3_out;

  or p0 (p0_out, in_2[0], in_2[1]);
  and g0 (g0_out, in_2[0], in_2[1]);
  or p1 (p1_out, in_2[2], in_2[3]);
  and g1 (g1_out, in_2[2], in_2[3]);
  or p2 (p2_out, in_2[4], in_2[5]);
  and g2 (g2_out, in_2[4], in_2[5]);
  or p3 (p3_out, in_2[6], in_2[7]);
  and g3 (g3_out, in_2[7], in_2[6]);
  and and_1 (and_1_out, C0, p0_out, p1_out, p2_out, p3_out);
  and and_2 (and_2_out, g0_out, p1_out, p2_out, p3_out);
  and and_3 (and_3_out, g1_out, p2_out, p3_out);
  and and_4 (and_4_out, g2_out, p3_out);
  or or_1 (C4, and_1_out, and_2_out, and_3_out, and_4_out, g3_out);
endmodule

module _4_bit_lookahead_adder (
  input  in_1,
  input  [7:0] in_2,
  output [3:0] out_3,
  output out_4,
  output out_5
);

  wire c1_1_out_3, c2_1_out_3;

  C1 c1_1 (.in_2(in_2), .in_1(in_1), .out_3(c1_1_out_3));
  C2 c2_1 (.in_2(in_2), .in_1(in_1), .out_3(c2_1_out_3));
  C3 c3_1 (.in_2(in_2), .in_1(in_1), .out_3(out_4));
  C4 c4_1 (.in_2(in_2), .C0(in_1), .C4(out_5));
  _1_bit_adder u_1_bit_adder_1 (.A(in_2[0]), .B(in_2[1]), .CARRY_IN(in_1), .SUM(out_3[0]));  // open: CARRY_OUT
  _1_bit_adder u_1_bit_adder_2 (.A(in_2[2]), .B(in_2[3]), .CARRY_IN(c1_1_out_3), .SUM(out_3[1]));  // open: CARRY_OUT
  _1_bit_adder u_1_bit_adder_3 (.A(in_2[4]), .B(in_2[5]), .CARRY_IN(c2_1_out_3), .SUM(out_3[2]));  // open: CARRY_OUT
  _1_bit_adder u_1_bit_adder_4 (.A(in_2[6]), .B(in_2[7]), .CARRY_IN(out_4), .SUM(out_3[3]));  // open: CARRY_OUT
endmodule

module _1_bit_adder (
  input  CARRY_IN,
  input  A,
  input  B,
  output SUM,
  output CARRY_OUT
);

  wire and_1_out, and_2_out, and_3_out;

  xor xor_1 (SUM, CARRY_IN, A, B);
  and and_1 (and_1_out, CARRY_IN, A);
  and and_2 (and_2_out, CARRY_IN, B);
  and and_3 (and_3_out, A, B);
  or or_1 (CARRY_OUT, and_1_out, and_2_out, and_3_out);
endmodule
